# Fritzing sketch ESP32CAM_SERVO_CAR (saved by Fritzing 0.9.3b)

parts:
  ESP32_-_Back1 = ESP32 - CAM
  S1 = H-Bridge with L298N
  J1 = Basic Servo
  J2 = Basic Servo
  M1 = DC Motor
  M2 = DC Motor
  M3 = DC Motor
  M4 = DC Motor
  VCC1 = Battery

nets:
  N1: ESP32_-_Back1.GPIO2, J2.pulse
  N2: ESP32_-_Back1.GPIO14, S1.IN1
  N3: ESP32_-_Back1.GPIO15, S1.IN2
  N4: ESP32_-_Back1.GPIO13, S1.IN3
  N5: ESP32_-_Back1.GPIO12, S1.IN4
  GND: ESP32_-_Back1.GND, S1.GND, J1.gnd, J2.gnd, VCC1.-
  5V: ESP32_-_Back1.5V, S1.5V, J1.vcc, J2.vcc
  N6: ESP32_-_Back1.GPIO3_/_RX, J1.pulse
  N7: S1.12V, VCC1.+
  N8: S1.M1-01, M3.pin_1, M4.pin_1
  N9: S1.M1-02, M3.pin_2, M4.pin_2
  N10: S1.M2-01, M1.pin_2, M2.pin_2
  N11: S1.M2-02, M1.pin_1, M2.pin_1

custom parts:
  ESP32 - CAM: The ESP32-CAM has a very competitive small-size camera module that can operate independently as a minimum system with a footprint of only 27*40.5*4.5mm and a deep sleep current of up to 6mA.
  H-Bridge with L298N: h-bridge
  Battery: Your standard 2x 18650 battery pack (7,4 Volts)
